// Logisim project LabArqui2.circ as structural Verilog: 4 circuits, main circuit main
module main (
  input  in_1,
  output [3:0] out_2
);

  wire clock_1_out, random_1_out;

  Clock clock_1 (.out(clock_1_out));
  Random #(.width(1)) random_1 (.clr(in_1), .clk(clock_1_out), .out(random_1_out));  // open: next
  BTS bts_1 (.X(random_1_out), .CLK(clock_1_out), .RESET(in_1), .STATE(out_2));  // open: S1, S2, S3
endmodule

module BTS (
  input  X,
  input  CLK,
  input  RESET,
  output S1,
  output S2,
  output S3,
  output [3:0] STATE
);

  wire statemachine_1_j0, statemachine_1_j1, statemachine_1_j2, statemachine_1_j3, statemachine_1_k0,
       statemachine_1_k1, statemachine_1_k2, statemachine_1_k3;

  StateMachine statemachine_1 (
    .Q3(STATE[3]), .Q2(STATE[2]), .Q1(STATE[1]), .Q0(STATE[0]), .X(X), .J3(statemachine_1_j3),
    .K3(statemachine_1_k3), .J2(statemachine_1_j2), .K2(statemachine_1_k2), .J1(statemachine_1_j1),
    .K1(statemachine_1_k1), .J0(statemachine_1_j0), .K0(statemachine_1_k0));
  J_K_Flip_Flop Q3 (
    .J(statemachine_1_j3), .K(statemachine_1_k3), .clk(CLK), .Q(STATE[3]), .reset(RESET));  // open: Qn, preset
  J_K_Flip_Flop Q2 (
    .J(statemachine_1_j2), .K(statemachine_1_k2), .clk(CLK), .Q(STATE[2]), .reset(RESET));  // open: Qn, preset
  J_K_Flip_Flop Q1 (
    .J(statemachine_1_j1), .K(statemachine_1_k1), .clk(CLK), .Q(STATE[1]), .reset(RESET));  // open: Qn, preset
  J_K_Flip_Flop Q0 (
    .J(statemachine_1_j0), .K(statemachine_1_k0), .clk(CLK), .Q(STATE[0]), .reset(RESET));  // open: Qn, preset
  SMRecognizer smrecognizer_1 (.Q3(STATE[3]), .Q2(STATE[2]), .Q1(STATE[1]), .Q0(STATE[0]), .S1(S1), .S2(S2), .S3(S3));
endmodule

module StateMachine (
  input  Q3,
  input  Q2,
  input  Q1,
  input  Q0,
  input  X,
  output J3,
  output K3,
  output J2,
  output K2,
  output J1,
  output K1,
  output J0,
  output K0
);

  wire and_1_out, and_2_out, and_3_out, and_4_out, and_5_out, and_6_out, and_7_out, and_8_out, and_9_out,
       and_10_out, and_11_out, and_12_out, and_13_out, and_15_out, and_16_out;

  and and_1 (and_1_out, Q2, ~Q1, X);  // AND_Gate
  and and_2 (and_2_out, Q1, ~X);  // AND_Gate
  and and_3 (and_3_out, ~Q2, Q1);  // AND_Gate
  and and_4 (and_4_out, ~Q2, ~X);  // AND_Gate
  and and_5 (and_5_out, Q2, Q1, X);
  and and_6 (and_6_out, ~Q2, ~Q1, X);  // AND_Gate
  and and_7 (and_7_out, X, Q3);
  and and_8 (and_8_out, ~Q3, Q2, Q0);  // AND_Gate
  and and_9 (and_9_out, Q2, ~X);  // AND_Gate
  and and_10 (and_10_out, Q0, X);
  and and_11 (and_11_out, Q0, Q2);
  or or_1 (J0, and_5_out, and_6_out, and_7_out);
  or or_2 (K0, and_1_out, and_2_out, and_3_out, and_4_out);
  or or_3 (K1, and_8_out, and_9_out);
  and and_12 (and_12_out, ~Q0, ~X);  // AND_Gate
  and and_13 (and_13_out, Q0, X);
  and and_14 (K2, ~Q1, Q0, X);  // AND_Gate
  or or_4 (J1, and_10_out, and_11_out);
  or or_5 (K3, Q1, and_12_out, and_13_out);
  and and_15 (and_15_out, Q2, ~Q1, ~Q0, X);  // AND_Gate
  and and_16 (and_16_out, Q2, ~Q1, Q0, ~X);  // AND_Gate
  or or_6 (J3, and_15_out, and_16_out);
  not not_1 (J2, X);
endmodule

module SMRecognizer (
  input  Q3,
  input  Q2,
  input  Q1,
  input  Q0,
  output S1,
  output S2,
  output S3
);

  and and_1 (S1, ~Q3, ~Q2, Q1, ~Q0);  // AND_Gate
  and and_2 (S2, Q3, Q2, Q1, Q0);
  and and_3 (S3, ~Q3, Q2, ~Q1, Q0);  // AND_Gate
endmodule
